# Fritzing sketch circuit-diagram (saved by Fritzing 0.9.3b)
circuit board: 15.9539cm x 9.92745cm
breadboards: 1

parts:
  元件2 = LED Matrix - Serial Interface - Red/Green/Blue
  元件1 = Arduino Uno (Rev3)
  LCM1602_IIC1 = LCM1602 IIC [part_number="LCM1602 IIC" chip_label="LCM1602 IIC" package="DIP (Dual Inline) [THT]"]
  LCD1 = LCD screen
  U1 = Thumb Joystick [package=joystick]

nets:
  VCC: 元件2.VCC, 元件1.5V, LCM1602_IIC1.VCC, U1.Y+
  GND: 元件2.GND, 元件1.GND, LCM1602_IIC1.GND, U1.X-, U1.V-
  N1: 元件2.MOSI, 元件1.D12/MISO
  N2: 元件2.CS, 元件1.D10_PWM/SS
  N3: 元件2.SCK, 元件1.D11_PWM/MOSI
  N4: 元件1.A0, U1.X
  N5: 元件1.A1, U1.Y
  N6: 元件1.A4/SDA, LCM1602_IIC1.SDA
  N7: 元件1.A5/SCL, LCM1602_IIC1.SCL
  N8: 元件1.D2, U1.SEL+
  VSS: LCM1602_IIC1.VSS, LCD1.VSS
  VDD: LCM1602_IIC1.VDD, LCD1.VDD
  N9: LCM1602_IIC1.V0, LCD1.V0
  N10: LCM1602_IIC1.RS, LCD1.RS
  N11: LCM1602_IIC1.RW, LCD1.R/W
  N12: LCM1602_IIC1.E, LCD1.E
  N13: LCM1602_IIC1.D0, LCD1.DB0
  N14: LCM1602_IIC1.D1, LCD1.DB1
  N15: LCM1602_IIC1.D2, LCD1.DB2
  N16: LCM1602_IIC1.D3, LCD1.DB3
  N17: LCM1602_IIC1.D4, LCD1.DB4
  N18: LCM1602_IIC1.D5, LCD1.DB5
  N19: LCM1602_IIC1.D6, LCD1.DB6
  N20: LCM1602_IIC1.D7, LCD1.DB7
  N21: LCM1602_IIC1.A, LCD1.LED+
  N22: LCM1602_IIC1.K, LCD1.LED-
  N23: LCM1602_IIC1.LED_A, LCM1602_IIC1.LED_B

custom parts:
  LCM1602 IIC: I2C-Module to use a 1602 or 2004 LCD on with the wire.h libory Serial LCD Modul
  Thumb Joystick: Thumb Joystick Joystick commonly found in PS2 controllers. Two pots and a select switch. Footprint proven. Spark Fun Electronics SKU : COM-09032
